# Fritzing sketch led_blink (saved by Fritzing 0.9.3b)
breadboards: 1

parts:
  Componente1 = Arduino Uno (Rev3)
  R1 = Resistor [tolerance=±5% resistance=220 package=THT]
  LED1 = LED - 5mm [color="Red (633nm)" package="5 mm [THT]"]

nets:
  N1: Componente1.D12/MISO, R1.Pin_1
  N2: Componente1.GND, LED1.cathode
  N3: R1.Pin_0, LED1.anode

// code stored in the sketch: led_blink.ino
/*
 *  Author: Guilherme Souza <gui.rsouza@gmail.com>
 *  
 *  This sketch blink a led connected in pin 13 of arduino with interval of 500mili
 */

// Arduino pin
int ledPin = 13;

/*
 * Setup: executed only once
 * Start ledPin for output sinal
 */
void setup() {
  pinMode(ledPin, OUTPUT);
}

/*
 * Loop: continues executing method
 * The principal commands and actions are write here, this is the 'body' of application
 */
void loop() {
  // light on led
  digitalWrite(ledPin, HIGH);
  // wait for 500 mili
  delay(500);
  // light off led
  digitalWrite(ledPin, LOW);
  // wait another 500 mili
  delay(500);
  
  // execute method 'loop' again
}
