# Fritzing sketch led_fade (saved by Fritzing 0.9.3b)
breadboards: 1

parts:
  R1 = Resistor [tolerance=±5% resistance=220 package=THT]
  LED1 = LED - 5mm [color="Red (633nm)" package="5 mm [THT]"]
  Componente1 = Arduino Uno (Rev3)

nets:
  N1: R1.Pin_0, LED1.anode
  N2: LED1.cathode, Componente1.GND

// code stored in the sketch: led_fade.ino
/*
 * Author: Guilherme Souza <gui.rsouza@gmail.com>
 *
 * This sketch give a animation of fade in Led's
 *
 */

int led = 5;

int brilho;

void setup() {
  pinMode(led, OUTPUT);
}

void loop() {
  
  // aumentar o brilho dos lEDs
  for (brilho = 0; brilho <= 255; brilho = brilho + 5) {
    analogWrite(led, brilho);
    // delay para atrasar momento fade
    delay(50);
  }

  // reduz o brilho dos lEDs
  for (brilho = 255; brilho >= 0; brilho = brilho - 5) {
    analogWrite(led, brilho);
    // delay para atrasar momento fade
    delay(50);
  }

}
